# Fritzing sketch TCC Diagram (saved by Fritzing 0.9.3b)
breadboards: 1

parts:
  YF-S201_Flow_Meter1 = YF-S201 Water Flow Meter
  Componente2 = Lilypad Battery Connect  # not connected
  Relay_Module = Keyes Relay [package=THT]
  Infrared_Relay = fc-51 [package=THT]
  Solenoid_Valve = Plastic Solenoid Valve
  J1 = 220v plug
  Componente3 = LCD1602-I2C
  U1 = ESP32-38PinWide [part_number=ESP32-38PinWide]

nets:
  N1: YF-S201_Flow_Meter1.SIG, Relay_Module.ground, Infrared_Relay.pin2, Componente3.GND, U1.GPIO11
  N2: YF-S201_Flow_Meter1.GND, U1.GPIO2
  VCC: YF-S201_Flow_Meter1.VCC, Componente3.VCC, U1.VIN
  N3: Relay_Module.signal, U1.GPIO23
  N4: Relay_Module.power, Infrared_Relay.pin3, U1.3.3
  N5: Relay_Module.C, J1.pin2
  N6: Relay_Module.NO, Solenoid_Valve.no_name_yet#1
  N7: Infrared_Relay.pin1, U1.GPIO4
  N8: Solenoid_Valve.no_name_yet#2, J1.pin1
  N9: Componente3.SDA, U1.GPIO21
  N10: Componente3.SCL, U1.GPIO22

notes:
  I2C Display
  ESP32

custom parts:
  YF-S201 Water Flow Meter: The YF-S201 Flow Meter. The input voltage is 5V to 24V (DC).
  Keyes Relay: The Keyes 5V relay module is suitable for SCM development, home appliance control. It uses a 5V~12V TIL control signal which can control DC / AC signal.
  220v plug: Generic 220V AC plug.
  LCD1602-I2C: A standard character display, usually with 2x16 characters. Comes in many colors with LCM1602 IIC attached.
  ESP32-38PinWide: Generic 38-Pin ESP32 with wide format (only access to one side of pins on a breadboard) based on Stephen Lilley's HiLetgo ESP-WROOM-32 ESP32 ESP-32S Development Board.
